# Fritzing sketch kalitka maketnaya (saved by Fritzing 0.9.3b)

parts:
  Часть1 = Arduino Uno (Rev3) - ICSP
  KEYPAD1 = Membrane Matrix Keypad
  J3 = Piezo Speaker
  J4 = Basic Servo
  hc-sr5 = hc-sr04
  S1 = Pushbutton [package="[THT]"]

nets (from the schematic view):
  VCC: Часть1.5V, J4.vcc, hc-sr5.VCC
  N1: Часть1.ICSP_MOSI, Часть1.D11_PWM/MOSI, KEYPAD1.2
  GND: Часть1.GND, J3.pin1, J4.gnd, hc-sr5.GND
  N2: Часть1.D8, KEYPAD1.5
  N3: Часть1.D9_PWM, KEYPAD1.4
  N4: Часть1.D10_PWM/SS, KEYPAD1.3
  N5: Часть1.D12/MISO, KEYPAD1.1
  N6: Часть1.D13/SCK, J3.pin2
  N7: Часть1.D2, hc-sr5.Echo
  N8: Часть1.D3_PWM, hc-sr5.Trig
  N9: Часть1.D4, J4.pulse
  N10: Часть1.D6_PWM, KEYPAD1.7
  N11: Часть1.D7, KEYPAD1.6
  N12: S1.Pin_1, S1.Pin_2

custom parts:
  Membrane Matrix Keypad: Membrane Matrix 3x4 Keypad
