# Fritzing sketch vorota maketnaya (saved by Fritzing 0.9.3b)
breadboards: 1

parts:
  LED1 = RGB LED (com. cathode, rgb) [package="5 mm [THT]"]
  SM1 = 28BYJ-48 Stepper Motor [part_number=28BYJ-48]
  Driver1 = 28BYJ-48 Driver Module [part_number=ULN2003 package=THT]
  OLED_I2C1 = OLED 128x64 I2C Monochrome Display
  hc-sr1 = hc-sr04
  Часть2 = RFID-RC522-v2
  Часть1 = Arduino Mega 2560 (Rev3)
  S1 = Pushbutton [package="[THT]"]
  S2 = Pushbutton [package="[THT]"]

nets (from the schematic view):
  N1: LED1.red_anode, Часть1.D4_PWM
  N2: LED1.green_anode, Часть1.D3_PWM
  N3: LED1.blue_anode, Часть1.D2_PWM
  N4: SM1.blue-pin, Driver1.blue-pin
  N5: SM1.pink-pin, Driver1.pink-pin
  N6: SM1.yellow-pin, Driver1.yellow-pin
  N7: SM1.orange-pin, Driver1.orange-pin
  N8: SM1.red-pin, Driver1.red-pin
  N9: Driver1.IN1, Часть1.D10_PWM
  N10: Driver1.IN2, Часть1.D11_PWM
  N11: Driver1.IN3, Часть1.D12_PWM
  N12: Driver1.IN4, Часть1.D13_PWM
  GND: Driver1.GND, OLED_I2C1.GND
  N13: OLED_I2C1.SDA, Часть1.D21/SCL
  N14: OLED_I2C1.SCK, Часть1.D20/SDA
  N15: hc-sr1.VCC, Часть1.IOREF
  N16: hc-sr1.Trig, Часть1.D43
  N17: hc-sr1.Echo, Часть1.D41
  N18: Часть2.SDA, Часть1.D9_PWM
  N19: Часть2.SCK, Часть1.D52
  N20: Часть2.MOSI, Часть1.D51
  N21: Часть2.MISO, Часть1.D50
  N22: Часть2.GND, Часть1.D8_PWM
  N23: Часть2.RST, Часть1.GND
  3.3V: Часть2.3.3V, Часть1.3V3
  N24: Часть1.D6_PWM, S1.Pin_3, S1.Pin_4
  N25: Часть1.D7_PWM, S2.Pin_4
  N26: S1.Pin_2, S2.Pin_2

custom parts:
  28BYJ-48 Stepper Motor: Unipolar Stepper Motor 28BYJ-48 Top coil - pink & orange Bottom coil - blue & yellow Common rail - red Connector pins: blue - pink - yellow - orange - red
  28BYJ-48 Driver Module: ULN2003 Driver Module for the 28BYJ-48 Unipolar Stepper Motor LED A - Blue wire - Bottom coil left LED B - Pink wire - Top coil left LED C - Yellow wire - Bottom coil right LED D - Orange wire - Top coil right Common rail - red Connector pins: blue - pink - yellow - orange - red Control pins - IN1 to IN4 Power pins - GND & Vmotor (5-12V) On/Off jumper (if removed, power to motor is cut).
  RFID-RC522-v2: A simple China made RFID-RC522 Reader; do check the pin labels, as this is a MFRC522 based clone.
